# Fritzing sketch 2RFID_ETHERNET_wV1 (saved by Fritzing 0.9.3b)
breadboards: 1

parts:
  Part2 = RFID-RC522 [part_number=101218]
  Part3 = RFID-RC522 [part_number=101218]
  Part4 = Arduino Ethernet Shield (Rev3)

nets:
  N1: Part2.SDA, Part4.PWM_D6
  N2: Part2.SCK, Part3.SCK, Part4.SPI/D13
  N3: Part2.MOSI, Part3.MOSI, Part4.PWM_D11
  N4: Part2.MISO, Part3.MISO, Part4.SPI/D12
  GND: Part2.GND, Part3.GND, Part4.GND
  N5: Part2.RST, Part3.RST, Part4.D2
  3.3V: Part2.3.3V, Part3.3.3V, Part4.3V3
  N6: Part3.SDA, Part4.PWM_D3

notes:
  ORANGE - D3 - RFID 0
  ORANGE - D6 - RFID 1
  GREEN - D13 - CLK/SCK
  YELLOW - D12 - MISO
  PURPLE - D11 - MOSI
  BROWN - D2 - RST
