# Fritzing sketch Base_Design (saved by Fritzing 0.9.3b)
breadboards: 1

parts:
  Part4 = RFID-RC522 [part_number=101218]
  Part5 = RFID-RC522 [part_number=101218]
  Part6 = Arduino Ethernet Shield (Rev3)

nets:
  N1: Part4.SDA, Part6.PWM_D9
  N2: Part4.SCK, Part5.SCK, Part6.SPI/D13
  N3: Part4.MOSI, Part5.MOSI, Part6.PWM_D11
  N4: Part4.MISO, Part5.MISO, Part6.SPI/D12
  GND: Part4.IRQ, Part4.GND, Part5.GND, Part6.GND
  N5: Part4.RST, Part5.RST, Part6.D8
  3.3V: Part4.3.3V, Part5.3.3V, Part6.3V3
  N6: Part5.SDA, Part6.PWM_D6

notes:
  SCK - BL
  MOSI - PURPLE
  MISO - GREEN
  SS - GREY
  RST - BROWN
  POWER 3.3v - RED
  GND- BLACK
  SCK - D13
  MOSI - D11
  MISO - D12
  RST -
  SS
  SS
  SLAVE 1 - RC 522
  SLAVE 2 - RC522
