# Fritzing sketch RFID_2LED_ARD (saved by Fritzing 0.9.3b)
breadboards: 1

parts:
  Part1 = Arduino Uno (Rev3)
  Part2 = RFID-RC522 [part_number=101218]
  R1 = Resistor [tolerance=±5% resistance=240 package="2010 [SMD]"]
  LED1 = smd LED [color="Yellow (595nm)" package="1206 [SMD]"]
  R2 = Resistor [tolerance=±5% resistance=240 package="2010 [SMD]"]
  LED2 = smd LED [color="Red (633nm)" package="0805 [SMD]"]

nets:
  N1: Part1.D9_PWM, Part2.RST
  N2: Part1.D10_PWM/SS, Part2.SDA
  N3: Part1.D11_PWM/MOSI, Part2.MOSI
  N4: Part1.D12/MISO, Part2.MISO
  N5: Part1.D13/SCK, Part2.SCK
  GND: Part1.GND, Part2.GND, LED1.anode, LED2.anode
  N6: Part1.D2, R1.Pin_0
  N7: Part1.D7, R2.Pin_1, LED2.cathode
  3V3: Part1.3V3, Part2.3.3V
  N8: R1.Pin_1, LED1.cathode
